// Logisim project hw5.circ as structural Verilog
module MyXOR (
  input  in_1,
  input  in_2,
  output out_3
);

  wire nand_1_out, nand_2_out, nand_3_out;

  nand nand_1 (nand_1_out, in_1, in_2);
  nand nand_2 (nand_2_out, in_1, nand_1_out);
  nand nand_3 (nand_3_out, nand_1_out, in_2);
  nand nand_4 (out_3, nand_2_out, nand_3_out, nand_3_out);

  // Notes on the sheet:
  //   Here is a location to build an XOR circuit
  //   You can follow the tutorial (Help menu - "tutorial") or work on your own...
endmodule

module FullAdder (
  input  X,
  input  Y,
  input  CarryIn,
  output sum,
  output CarryOut
);

  wire and_1_out, and_2_out, nand_1_out, nand_2_out, nand_3_out, nand_4_out, nand_5_out, nand_6_out,
       nand_7_out;

  nand nand_1 (nand_1_out, X, Y);
  and and_1 (and_1_out, Y, X);
  and and_2 (and_2_out, nand_5_out, CarryIn, CarryIn);
  nand nand_2 (nand_2_out, X, nand_1_out);
  nand nand_3 (nand_3_out, nand_1_out, Y);
  nand nand_4 (nand_4_out, nand_5_out, CarryIn);
  nand nand_5 (nand_5_out, nand_2_out, nand_3_out, nand_3_out);
  nand nand_6 (nand_6_out, nand_5_out, nand_4_out);
  nand nand_7 (nand_7_out, nand_4_out, CarryIn);
  nand nand_8 (sum, nand_6_out, nand_7_out, nand_7_out);
  or or_1 (CarryOut, and_1_out, and_2_out, and_2_out);
endmodule

module _4_bit_Ripple_Carry_Adder (
  input  Y3,
  input  Y2,
  input  Y1,
  input  Y0,
  input  X3,
  input  X2,
  input  X1,
  input  X0,
  output Sum4,
  output Sum3,
  output Sum2,
  output Sum1,
  output Sum0
);

  wire fulladder_2_carryout, fulladder_3_carryout, fulladder_4_carryout;

  FullAdder fulladder_1 (.X(Y3), .Y(X3), .CarryIn(fulladder_2_carryout), .sum(Sum3), .CarryOut(Sum4));
  FullAdder fulladder_2 (.X(Y2), .Y(X2), .CarryIn(fulladder_3_carryout), .sum(Sum2), .CarryOut(fulladder_2_carryout));
  FullAdder fulladder_3 (.X(Y1), .Y(X1), .CarryIn(fulladder_4_carryout), .sum(Sum1), .CarryOut(fulladder_3_carryout));
  FullAdder fulladder_4 (.X(Y0), .Y(X0), .CarryIn(1'b0), .sum(Sum0), .CarryOut(fulladder_4_carryout));
endmodule

module _4_bit_Multiplier (
  input  Y3,
  input  Y2,
  input  Y1,
  input  Y0,
  input  X0,
  input  X1,
  input  X2,
  input  X3,
  output Z0,
  output Z1,
  output Z2,
  output Z3,
  output Z4,
  output Z5,
  output Z6,
  output Z7
);

  wire n4_bit_ripple_carry_adder_1_sum1, n4_bit_ripple_carry_adder_1_sum2, n4_bit_ripple_carry_adder_1_sum3,
       n4_bit_ripple_carry_adder_1_sum4, n4_bit_ripple_carry_adder_2_sum1, n4_bit_ripple_carry_adder_2_sum2,
       n4_bit_ripple_carry_adder_2_sum3, n4_bit_ripple_carry_adder_2_sum4, n4x1_bit_multiplier_1_z2,
       n4x1_bit_multiplier_1_z3, n4x1_bit_multiplier_1_z4, n4x1_bit_multiplier_2_z1,
       n4x1_bit_multiplier_2_z2, n4x1_bit_multiplier_2_z3, n4x1_bit_multiplier_2_z4,
       n4x1_bit_multiplier_3_z1, n4x1_bit_multiplier_3_z2, n4x1_bit_multiplier_3_z3,
       n4x1_bit_multiplier_3_z4, n4x1_bit_multiplier_4_z1, n4x1_bit_multiplier_4_z2,
       n4x1_bit_multiplier_4_z3, n4x1_bit_multiplier_4_z4;

  _4x1_Bit_Multiplier u_4x1_bit_multiplier_1 (
    .Z1(Z0), .Z2(n4x1_bit_multiplier_1_z2), .Z3(n4x1_bit_multiplier_1_z3), .Z4(n4x1_bit_multiplier_1_z4),
    .Y0(Y0), .Y1(Y1), .Y2(Y2), .Y3(Y3), .X0(X0));
  _4x1_Bit_Multiplier u_4x1_bit_multiplier_2 (
    .Z1(n4x1_bit_multiplier_2_z1), .Z2(n4x1_bit_multiplier_2_z2), .Z3(n4x1_bit_multiplier_2_z3),
    .Z4(n4x1_bit_multiplier_2_z4), .Y0(Y0), .Y1(Y1), .Y2(Y2), .Y3(Y3), .X0(X1));
  _4_bit_Ripple_Carry_Adder u_4_bit_ripple_carry_adder_1 (
    .Y3(1'b0), .X3(n4x1_bit_multiplier_2_z4), .Y2(n4x1_bit_multiplier_1_z4), .X2(n4x1_bit_multiplier_2_z3),
    .Y1(n4x1_bit_multiplier_1_z3), .X1(n4x1_bit_multiplier_2_z2), .Y0(n4x1_bit_multiplier_1_z2),
    .X0(n4x1_bit_multiplier_2_z1), .Sum4(n4_bit_ripple_carry_adder_1_sum4),
    .Sum3(n4_bit_ripple_carry_adder_1_sum3), .Sum2(n4_bit_ripple_carry_adder_1_sum2),
    .Sum1(n4_bit_ripple_carry_adder_1_sum1), .Sum0(Z1));
  _4x1_Bit_Multiplier u_4x1_bit_multiplier_3 (
    .Z1(n4x1_bit_multiplier_3_z1), .Z2(n4x1_bit_multiplier_3_z2), .Z3(n4x1_bit_multiplier_3_z3),
    .Z4(n4x1_bit_multiplier_3_z4), .Y0(Y0), .Y1(Y1), .Y2(Y2), .Y3(Y3), .X0(X2));
  _4_bit_Ripple_Carry_Adder u_4_bit_ripple_carry_adder_2 (
    .Y3(n4_bit_ripple_carry_adder_1_sum4), .X3(n4x1_bit_multiplier_3_z4),
    .Y2(n4_bit_ripple_carry_adder_1_sum3), .X2(n4x1_bit_multiplier_3_z3),
    .Y1(n4_bit_ripple_carry_adder_1_sum2), .X1(n4x1_bit_multiplier_3_z2),
    .Y0(n4_bit_ripple_carry_adder_1_sum1), .X0(n4x1_bit_multiplier_3_z1),
    .Sum4(n4_bit_ripple_carry_adder_2_sum4), .Sum3(n4_bit_ripple_carry_adder_2_sum3),
    .Sum2(n4_bit_ripple_carry_adder_2_sum2), .Sum1(n4_bit_ripple_carry_adder_2_sum1), .Sum0(Z2));
  _4x1_Bit_Multiplier u_4x1_bit_multiplier_4 (
    .Z1(n4x1_bit_multiplier_4_z1), .Z2(n4x1_bit_multiplier_4_z2), .Z3(n4x1_bit_multiplier_4_z3),
    .Z4(n4x1_bit_multiplier_4_z4), .Y0(Y0), .Y1(Y1), .Y2(Y2), .Y3(Y3), .X0(X3));
  _4_bit_Ripple_Carry_Adder u_4_bit_ripple_carry_adder_3 (
    .Y3(n4_bit_ripple_carry_adder_2_sum4), .X3(n4x1_bit_multiplier_4_z4),
    .Y2(n4_bit_ripple_carry_adder_2_sum3), .X2(n4x1_bit_multiplier_4_z3),
    .Y1(n4_bit_ripple_carry_adder_2_sum2), .X1(n4x1_bit_multiplier_4_z2),
    .Y0(n4_bit_ripple_carry_adder_2_sum1), .X0(n4x1_bit_multiplier_4_z1), .Sum4(Z7), .Sum3(Z6), .Sum2(Z5),
    .Sum1(Z4), .Sum0(Z3));

  // Notes on the sheet:
  //   factor (4 bits)
  //   See the problem for details on this hint: perhaps build a 4x1-bit multiplier first!
  //   second factor (4 bits)
  //   product (8 bits)
  //   least sig
  //   most sig
endmodule

module _3by2_divider (
  input  Y2,
  input  Y1,
  input  Y0,
  input  X1,
  input  X0,
  output Z2,
  output Z1,
  output Z0,
  output Error
);


  // Notes on the sheet:
  //   Dividend (3 bits: Y2 Y1 Y0)
  //   Divisor (2 bits: X1 X0)
  //   Quotient (4 bits: Z2 Z1 Z0 and Error)
endmodule

module _4x1_Bit_Multiplier (
  input  X0,
  input  Y0,
  input  Y1,
  input  Y2,
  input  Y3,
  output Z1,
  output Z2,
  output Z3,
  output Z4
);

  and and_1 (Z1, Y0, X0);
  and and_2 (Z2, Y1, X0);
  and and_3 (Z3, Y2, X0);
  and and_4 (Z4, Y3, X0);
endmodule
